# Fritzing sketch SolarTracket (saved by Fritzing 0.9.3b)
breadboards: 2

parts:
  Componente1 = Arduino Uno (Rev3)
  R4 = Resistor [tolerance=±5% resistance=10k package=THT]
  LDR1 = Photocell (LDR) [package=THT]
  R10 = Resistor [tolerance=±5% resistance=10k package=THT]
  R11 = Resistor [tolerance=±5% resistance=10k package=THT]
  R12 = Resistor [tolerance=±5% resistance=10k package=THT]
  LDR2 = Photocell (LDR) [package=THT]
  LDR3 = Photocell (LDR) [package=THT]
  LDR4 = Photocell (LDR) [package=THT]
  R16 = Resistor [tolerance=±5% resistance=1k package=THT]
  R17 = Resistor [tolerance=±5% resistance=220 package=THT]
  R20 = Resistor [tolerance=±5% resistance=220 package=THT]
  R22 = Resistor [tolerance=±5% resistance=220 package=THT]
  R23 = Resistor [tolerance=±5% resistance=220 package=THT]
  R24 = Resistor [tolerance=±5% resistance=220 package=THT]
  LED1 = LED - 5mm [color="Blue (430nm)" package="5 mm [THT]"]
  LED2 = LED - 5mm [color="Blue (430nm)" package="5 mm [THT]"]
  LED3 = LED - 5mm [color="Blue (430nm)" package="5 mm [THT]"]
  LED4 = LED - 5mm [color="Blue (430nm)" package="5 mm [THT]"]
  LED5 = LED - 5mm [color="Blue (430nm)" package="5 mm [THT]"]
  R25 = Resistor [tolerance=±5% resistance=220 package=THT]
  LED6 = LED - 5mm [color="Blue (430nm)" package="5 mm [THT]"]
  J1 = Basic Servo
  J2 = Basic Servo
  Q1 = Basic FET N-Channel [package="TO220 [THT]"]

nets:
  N1: Componente1.A0, R4.Pin_0, LDR1.pin_0
  N2: Componente1.A1, R10.Pin_0, LDR2.pin_0
  N3: Componente1.A2, R12.Pin_0, LDR3.pin_0
  N4: Componente1.A3, R11.Pin_0, LDR4.pin_0
  GND: Componente1.GND, R4.Pin_1, R10.Pin_1, R11.Pin_1, R12.Pin_1, J1.gnd, J2.gnd, Q1.source
  N5: Componente1.D5_PWM, J2.pulse
  N6: Componente1.D6_PWM, J1.pulse
  N7: Componente1.D7, R16.Pin_0
  VCC: Componente1.5V, LDR1.pin_1, LDR2.pin_1, LDR3.pin_1, LDR4.pin_1, LED1.anode, LED2.anode, LED3.anode, LED4.anode, LED5.anode, LED6.anode, J1.vcc, J2.vcc
  N8: R16.Pin_1, Q1.gate
  N9: R17.Pin_0, LED1.cathode
  N10: R17.Pin_1, R20.Pin_1, R22.Pin_1, R23.Pin_1, R24.Pin_1, R25.Pin_1, Q1.drain
  N11: R20.Pin_0, LED2.cathode
  N12: R22.Pin_0, LED3.cathode
  N13: R23.Pin_0, LED4.cathode
  N14: R24.Pin_0, LED5.cathode
  N15: R25.Pin_0, LED6.cathode
